# Fritzing sketch capacitive (saved by Fritzing 0.8.3b)
breadboards: 1

parts:
  LED1 = LED - 5mm [color="Green (555nm)" package="5 mm [THT]"]
  LED2 = LED - 5mm [color="Red (633nm)" package="5 mm [THT]"]
  LED3 = LED - 5mm [color="Yellow (595nm)" package="5 mm [THT]"]
  R1 = Resistor [tolerance=±5% resistance=1M package=THT]
  R2 = Resistor [tolerance=±5% resistance=1M package=THT]
  R4 = Resistor [tolerance=±5% resistance=220 package=THT]
  R5 = Resistor [tolerance=±5% resistance=220 package=THT]
  Parte1 = Arduino Uno (Rev3)
  R6 = Resistor [tolerance=±5% resistance=1M package=THT]
  R7 = Resistor [tolerance=±5% resistance=220 package=THT]

nets:
  N1: LED1.cathode, R5.Pin_1
  N2: LED1.anode, Parte1.D10_PWM/SS
  N3: LED2.cathode, R7.Pin_1
  N4: LED2.anode, Parte1.D8
  N5: LED3.cathode, R4.Pin_1
  N6: LED3.anode, Parte1.D9_PWM
  N7: R1.Pin_0, R2.Pin_0, Parte1.D2, R6.Pin_0
  N8: R1.Pin_1, Parte1.D7
  N9: R2.Pin_1, Parte1.D5_PWM
  N10: R4.Pin_0, R5.Pin_0, Parte1.GND, R7.Pin_0
  N11: Parte1.D6_PWM, R6.Pin_1

notes:
  Aluminio
